// Logisim project MY4BITcpu.circ as structural Verilog: 2 circuits, main circuit main
module main (
  input  KEEP_AT_1,
  output [3:0] OUTPUT
);

  wire CLK_out, demultiplexer_1_out1, demultiplexer_1_out2, demultiplexer_1_out3, demultiplexer_1_out4,
       multiplexer_8_out, RESET_ADDR_out;
  wire [3:0] ALU_output, multiplexer_1_out, multiplexer_2_out, multiplexer_3_out, multiplexer_4_out,
       multiplexer_5_out, multiplexer_6_out, multiplexer_7_out, R0_q, R1_q, R2_q, R3_q, rom_1_data,
       rom_1_data_2, rom_1_data_3, rom_1_data_4;
  wire [6:0] counter_1_q;

  Multiplexer #(.select(4), .width(4)) multiplexer_1 (
    .in1(multiplexer_7_out), .out(multiplexer_1_out), .sel(rom_1_data));  // open: in0, in2, in3, in4, in5, in6, in7, in8, in9, in10, in11, in12, in13, in14, in15, en
  Multiplexer #(.select(4), .width(4)) multiplexer_2 (
    .in2(multiplexer_7_out), .out(multiplexer_2_out), .sel(rom_1_data));  // open: in0, in1, in3, in4, in5, in6, in7, in8, in9, in10, in11, in12, in13, in14, in15, en
  Multiplexer #(.select(4), .width(4)) multiplexer_3 (
    .in3(multiplexer_7_out), .out(multiplexer_3_out), .sel(rom_1_data));  // open: in0, in1, in2, in4, in5, in6, in7, in8, in9, in10, in11, in12, in13, in14, in15, en
  Multiplexer #(.select(4), .width(4)) multiplexer_4 (
    .in4(multiplexer_7_out), .out(multiplexer_4_out), .sel(rom_1_data));  // open: in0, in1, in2, in3, in5, in6, in7, in8, in9, in10, in11, in12, in13, in14, in15, en
  Counter #(.width(7), .max('h7f)) counter_1 (
    .Q(counter_1_q), .clk(CLK_out), .clr(RESET_ADDR_out));  // open: load, D, count, carry
  Button RESET_ADDR (.out(RESET_ADDR_out));
  Clock CLK (.out(CLK_out));
  ROM #(.addrWidth(7), .dataWidth(16)) rom_1 (
    .addr(counter_1_q), .data({rom_1_data_4, rom_1_data_3, rom_1_data_2, rom_1_data}));  // open: sel
  Register #(.width(4)) R0 (.D(multiplexer_1_out), .Q(R0_q), .clk(CLK_out), .clr(demultiplexer_1_out1));  // open: en
  Register #(.width(4)) R1 (.D(multiplexer_2_out), .Q(R1_q), .clk(CLK_out), .clr(demultiplexer_1_out2));  // open: en
  Register #(.width(4)) R2 (.D(multiplexer_3_out), .Q(R2_q), .clk(CLK_out), .clr(demultiplexer_1_out3));  // open: en
  Register #(.width(4)) R3 (.D(multiplexer_4_out), .Q(R3_q), .clk(CLK_out), .clr(demultiplexer_1_out4));  // open: en
  Multiplexer #(.select(4), .width(4)) multiplexer_5 (
    .in1(R0_q), .in2(R1_q), .in3(R2_q), .in4(R3_q), .out(multiplexer_5_out), .sel(rom_1_data_2));  // open: in0, in5, in6, in7, in8, in9, in10, in11, in12, in13, in14, in15, en
  Multiplexer #(.select(4), .width(4)) multiplexer_6 (
    .in1(R0_q), .in2(R1_q), .in3(R2_q), .in4(R3_q), .out(multiplexer_6_out), .sel(rom_1_data));  // open: in0, in5, in6, in7, in8, in9, in10, in11, in12, in13, in14, in15, en
  Multiplexer #(.select(4), .width(4)) multiplexer_7 (
    .in1(multiplexer_5_out), .in4(OUTPUT), .in5(rom_1_data_2), .out(multiplexer_7_out), .sel(rom_1_data_3));  // open: in0, in2, in3, in6, in7, in8, in9, in10, in11, in12, in13, in14, in15, en
  Multiplexer #(.select(4)) multiplexer_8 (
    .in2(KEEP_AT_1), .out(multiplexer_8_out), .sel(rom_1_data_3));  // open: in0, in1, in3, in4, in5, in6, in7, in8, in9, in10, in11, in12, in13, in14, in15, en
  Demultiplexer #(.select(4)) demultiplexer_1 (
    .out1(demultiplexer_1_out1), .out2(demultiplexer_1_out2), .out3(demultiplexer_1_out3),
    .out4(demultiplexer_1_out4), .in(multiplexer_8_out), .sel(rom_1_data));  // open: out0, out5, out6, out7, out8, out9, out10, out11, out12, out13, out14, out15, en
  ALU ALU (.N1(multiplexer_5_out), .N2(multiplexer_6_out), .OPCODE(rom_1_data_4), .OUTPUT(ALU_output));
  Register #(.width(4)) register_1 (.D(ALU_output), .Q(OUTPUT), .clk(CLK_out));  // open: en, clr

  // Notes on the sheet:
  //   ROM PLACE YOUR COMPILED PROGRAMS HERE
  //   contents of rom_1 (hex, n*v repeats v):
  //   542 523 1023 404
  //   reg hex
  //   final hex
endmodule

module ALU (
  input  [3:0] N1,
  input  [3:0] N2,
  input  [3:0] OPCODE,
  output [3:0] OUTPUT
);

  wire [3:0] adder_1_out, divider_1_out, multiplier_1_out, subtractor_1_out;

  Adder #(.width(4)) adder_1 (.a(N1), .b(N2), .out(adder_1_out));  // open: cin, cout
  Subtractor #(.width(4)) subtractor_1 (.a(N1), .b(N2), .out(subtractor_1_out));  // open: bin, bout
  Multiplier #(.width(4)) multiplier_1 (.a(N1), .b(N2), .out(multiplier_1_out));  // open: cin, cout
  Divider #(.width(4)) divider_1 (.a(N1), .b(N2), .out(divider_1_out));  // open: upper, rem
  Multiplexer #(.select(4), .width(4)) multiplexer_1 (
    .in1(adder_1_out), .in2(subtractor_1_out), .in3(multiplier_1_out), .in4(divider_1_out), .out(OUTPUT),
    .sel(OPCODE));  // open: in0, in5, in6, in7, in8, in9, in10, in11, in12, in13, in14, in15, en
endmodule
